# Fritzing sketch Transmitter (saved by Fritzing 0.9.3b)

parts:
  Part1 = Arduino Uno (Rev3)
  S1 = Pushbutton [package="[SMD]"]
  Mod1 = KY-008 Laser Transmitter Module [package="Breakout board"]

nets:
  N1: Part1.D2, Mod1.S
  N2: Part1.D3_PWM, S1.Pin_1
  N3: Part1.GND, S1.Pin_3, S1.Pin_4, Mod1.-

custom parts:
  KY-008 Laser Transmitter Module: KY-008 Laser Transmitter Module, emits a dot shaped red laser beam.

// code stored in the sketch: transmitter.ino
#define POT_PIN A0
#define OUTPUT_PIN 2
#define SIGNAL_PIN 3

uint8_t potValue;
void sendThroughLaser (const byte, uint8_t);

void setup ()
{
	Serial.begin (9600);
	pinMode (POT_PIN, INPUT);
	pinMode (OUTPUT_PIN, OUTPUT);
	pinMode (SIGNAL_PIN, INPUT_PULLUP);
	digitalWrite (OUTPUT_PIN, LOW);
}

void loop ()
{
	while (digitalRead (SIGNAL_PIN));

	potValue = map (analogRead (POT_PIN), 0, 1023, 0, 255);
	sendThroughLaser (OUTPUT_PIN, potValue);
	delay (20);
}

void sendThroughLaser (const byte outputPin, uint8_t dataToSend)
{
	bool currentOutputState = LOW;
	uint8_t temp = dataToSend;
	for (int i = 0; i < 8; i++){
		digitalWrite (outputPin, !currentOutputState);
		delay (5); //signalling new bit
		currentOutputState = temp & B00000001;	//access LSB of data
		temp >>= 1;
		digitalWrite (outputPin, currentOutputState);	
		delay (10);
		Serial.println (currentOutputState);
	}
	digitalWrite (outputPin, LOW);
	Serial.println (dataToSend, BIN);
}
