# Fritzing sketch Reciever (saved by Fritzing 0.9.3b)

parts:
  Part5 = Arduino Nano (Rev3.0) (ICSP)
  M3 = Getriebemotor
  M4 = Getriebemotor
  IC2 = L293D [package=THT]
  VCC2 = 4 x AAA Battery Mount
  J2 = Basic Servo
  hc-sr2 = hc-sr04
  DHT2 = DHT11 Humitidy and Temperature Sensor
  Part6 = NRF24L01+ Breakout Board
  C1 = Electrolytic Capacitor [capacitance=0.1mF package="100 mil [THT, electrolytic]"]

nets:
  N1: Part5.D3, J2.pulse
  N2: Part5.D5, IC2.Enable_1
  N3: Part5.D6, IC2.Enable_2
  N4: Part5.D7, Part6.CE
  N5: Part5.D8, Part6.CS
  GND: Part5.GND, J2.gnd, hc-sr2.GND, DHT2.GND, Part6.GND, C1.-
  VCC: Part5.5V, IC2.+V, J2.vcc, hc-sr2.VCC, DHT2.VDD
  N6: Part5.A7, hc-sr2.Trig
  N7: Part5.A6, hc-sr2.Echo
  N8: Part5.A5, DHT2.DATA
  N9: Part5.A4, IC2.In_3
  N10: Part5.A3, IC2.In_4
  N11: Part5.A2, IC2.In_1
  N12: Part5.A1, IC2.In_2
  3V3: Part5.3V3, Part6.VCC, C1.+
  N13: Part5.D12/MISO, Part6.MISO
  N14: Part5.D13/SCK, Part6.SCK
  N15: Part5.D11/MOSI, Part6.MOSI
  N16: M3.pin_1, IC2.Out_4_(_Controlled_by_Enable_2_)
  N17: M3.pin_2, IC2.Out_3_(_Controlled_by_Enable_2_)
  N18: M4.pin_1, IC2.Out_2_(_Controlled_by_Enable_1_)
  N19: M4.pin_2, IC2.Out_1_(_Controlled_by_Enable_1_)
  N20: IC2.0V, VCC2.-
  N21: IC2.+Vmotor, VCC2.+

custom parts:
  DHT11 Humitidy and Temperature Sensor: DHT11 Humidity and Temperature Sensor
