# Fritzing sketch Transmitter (saved by Fritzing 0.9.3b)

parts:
  Part1 = NRF24L01+ Breakout Board
  Part2 = Arduino Uno (Rev3) - ICSP
  Part3 = LCD1602-I2C
  Part4 = Thumb Joystick
  Part5 = Thumb Joystick
  RE2 = Rotary Encoder [package=THT]
  R1 = Resistor [tolerance=±5% resistance=10k package=THT]
  R2 = Resistor [tolerance=±5% resistance=10k package=THT]

nets:
  GND: Part1.GND, Part2.GND, Part3.GND, Part4.GND, Part5.GND, RE2.EncoderPinC
  VCC: Part1.VCC, Part2.3V3
  N1: Part1.CE, Part2.D7
  N2: Part1.CS, Part2.D8
  N3: Part1.SCK, Part2.ICSP_SCK
  N4: Part1.MOSI, Part2.ICSP_MOSI
  N5: Part1.MISO, Part2.ICSP_MISO
  N6: Part2.A0, Part5.HORZ
  N7: Part2.A1, Part5.VERT
  N8: Part2.A2, Part4.HORZ
  N9: Part2.A3, Part4.VERT
  N10: Part2.A4/SDA, Part3.SDA
  N11: Part2.A5/SCL, Part3.SCL
  N12: Part2.D2, RE2.EncoderPinB, R2.Pin_0
  N13: Part2.D3_PWM, RE2.EncoderPinA, R1.Pin_1
  VCC_2: Part2.5V, Part3.VCC, Part4.VCC, Part5.VCC, R1.Pin_0, R2.Pin_1

custom parts:
  LCD1602-I2C: A standard character display, usually with 2x16 characters. Comes in many colors with LCM1602 IIC attached.
