# Fritzing sketch Timer (saved by Fritzing 0.9.3b)

parts:
  Part1 = Arduino Nano (Rev3.0) (ICSP)
  Strt/Stp = Pushbutton [package="[THT]"]
  Field = Pushbutton [package="[THT]"]
  Value_(-) = Pushbutton [package="[THT]"]
  Value_(+) = Pushbutton [package="[THT]"]
  J1 = Piezo Speaker
  R1 = Resistor [tolerance=±5% resistance=220 package=THT]
  Sound_Enable = SWITCH_SPDT [package=kps-1290]
  Part2 = LCD1602-I2C

nets:
  N1: Part1.D2, Strt/Stp.Pin_1
  N2: Part1.D3, Value_(-).Pin_1, Value_(-).Pin_2
  N3: Part1.D4, Value_(+).Pin_1, Value_(+).Pin_2
  N4: Part1.D5, Field.Pin_1, Field.Pin_2
  N5: Part1.D6, J1.pin2, R1.Pin_0
  N6: Part1.D7, Sound_Enable.O
  GND: Part1.GND, Part2.GND
  5V: Part1.5V, Part2.VCC
  N7: Part1.A5, Part2.SDA
  N8: Part1.A4, Part2.SCL
  N9: Strt/Stp.Pin_3, Strt/Stp.Pin_4, Field.Pin_3, Field.Pin_4, Value_(-).Pin_3, Value_(-).Pin_4, Value_(+).Pin_4, R1.Pin_1, Sound_Enable.P

custom parts:
  LCD1602-I2C: A standard character display, usually with 2x16 characters. Comes in many colors with LCM1602 IIC attached.
